# Fritzing sketch protype1 (saved by Fritzing 0.9.3b)
circuit board: 8.46667cm x 5.64444cm
breadboards: 1

parts:
  Q5 = NPN-Transistor [package="TO92 [THT]"]
  Q8 = PNP-Transistor [package="TO92 [THT]"]
  Q7 = NPN-Transistor [package="TO92 [THT]"]
  Q6 = PNP-Transistor [package="TO92 [THT]"]
  R9 = Resistor [tolerance=±5% resistance=2k package=THT]
  R6 = Resistor [tolerance=±5% resistance=100k package=THT]
  R7 = Resistor [tolerance=±5% resistance=100k package=THT]
  R8 = Resistor [tolerance=±5% resistance=100k package=THT]
  R5 = Resistor [tolerance=±5% resistance=100k package=THT]
  LED1 = LED - 5mm [color="Red (633nm)" package="5 mm [THT]"]
  LED2 = LED - 5mm [color="Red (633nm)" package="5 mm [THT]"]
  Q4 = NPN-Transistor [package="TO92 [THT]"]
  Q2 = NPN-Transistor [package="TO92 [THT]"]
  R4 = Resistor [tolerance=±5% resistance=3.9k package=THT]
  R2 = Resistor [tolerance=±5% resistance=3.9k package=THT]
  J1 = female pin header, 2 pins [form="♀ (female)"]
  J2 = female pin header, 2 pins [form="♀ (female)"]
  Q3 = PNP-Transistor [package="TO92 [THT]"]
  Q1 = PNP-Transistor [package="TO92 [THT]"]
  R1 = Resistor [tolerance=±5% resistance=3.9k package=THT]
  R3 = Resistor [tolerance=±5% resistance=3.9k package=THT]

nets:
  GND: Q5.E, Q7.E, Q4.E, Q2.E
  N1: Q5.B, R5.Pin_1
  N2: Q5.C, Q8.C, J2.pin1
  30V: Q8.E, Q6.E, Q3.E, Q1.E
  N3: Q8.B, R8.Pin_1
  N4: Q7.B, R7.Pin_0
  N5: Q7.C, Q6.C, J1.pin2
  N6: Q6.B, R6.Pin_0
  N7: R9.Pin_0, LED1.anode, LED2.cathode
  N8: R9.Pin_1, J1.pin1
  N9: R6.Pin_1, Q2.C
  N10: R7.Pin_1, Q3.C
  N11: R8.Pin_0, Q4.C
  N12: R5.Pin_0, Q1.C
  N13: LED1.cathode, LED2.anode, J2.pin2
  N14: Q4.B, R4.Pin_1
  N15: Q2.B, R2.Pin_0
  GPIO23: R4.Pin_0
  GPIO18: R2.Pin_1
  N16: Q3.B, R3.Pin_0
  N17: Q1.B, R1.Pin_1
  GPIO17: R1.Pin_0
  GPIO22: R3.Pin_1
